# Fritzing sketch BoardGame (saved by Fritzing 0.9.2b)
circuit board: 20cm x 16.7cm
breadboards: 4

parts:
  MAX7219 = MAX7219 [package=dil24]
  C1 = Ceramic Capacitor [capacitance=100nF package="100 mil [THT, multilayer]"]
  C2 = Electrolytic Capacitor [capacitance=10µF package="100 mil [THT, electrolytic]"]
  R1 = Resistor [tolerance=±5% resistance=100k package=THT]
  C3 = Electrolytic Capacitor [capacitance=10µF package="100 mil [THT, electrolytic]"]
  LM7805 = Voltage Regulator - 5V [package="TO220 [THT]"]
  C4 = Electrolytic Capacitor [capacitance=10µF package="100 mil [THT, electrolytic]"]
  -5V+ = Generic female header - 2 pins [form="♀ (female)" package=THT]
  R2 = Resistor [tolerance=±5% resistance=10k package=THT]
  R3 = Resistor [tolerance=±5% resistance=10k package=THT]
  R4 = Resistor [tolerance=±5% resistance=10k package=THT]
  R5 = Resistor [tolerance=±5% resistance=10k package=THT]
  C6 = Ceramic Capacitor [capacitance=10nF package="100 mil [THT, multilayer]"]
  LedRing = Led ring header [package=THT]
  R6 = Resistor [tolerance=±5% resistance=1k package=THT]
  R7 = Resistor [tolerance=±5% resistance=1k package=THT]
  Rotary = Rotary Encoder [package=THT]
  R8 = Resistor [tolerance=±5% resistance=47k package=THT]
  R9 = Resistor [tolerance=±5% resistance=68k package=THT]
  R10 = Resistor [tolerance=±5% resistance=47k package=THT]
  R11 = Resistor [tolerance=±5% resistance=68k package=THT]
  USB_Charger = USB Connectors [part_number=bt package=usb-a-h]
  +_IN_- = screw terminal, 2 pins
  D1 = Diode [package=diode-1n4001]
  USB_Battery = USB Connectors [part_number=bt package=usb-a-h]
  Sw_DC = screw terminal, 2 pins
  Sw_Batt = screw terminal, 2 pins
  LED1 = LED - 5mm [color="Red (633nm)" package="5 mm [THT]"]
  LED2 = LED - 5mm [color="Red (633nm)" package="5 mm [THT]"]
  LED3 = LED - 5mm [color="Red (633nm)" package="5 mm [THT]"]
  LED4 = LED - 5mm [color="Red (633nm)" package="5 mm [THT]"]
  LED5 = LED - 5mm [color="Red (633nm)" package="5 mm [THT]"]
  LED6 = LED - 5mm [color="Red (633nm)" package="5 mm [THT]"]
  LED7 = LED - 5mm [color="Red (633nm)" package="5 mm [THT]"]
  LED8 = LED - 5mm [color="Red (633nm)" package="5 mm [THT]"]
  LED9 = LED - 5mm [color="Red (633nm)" package="5 mm [THT]"]
  LED10 = LED - 5mm [color="Red (633nm)" package="5 mm [THT]"]
  LED11 = LED - 5mm [color="Red (633nm)" package="5 mm [THT]"]
  LED12 = LED - 5mm [color="Red (633nm)" package="5 mm [THT]"]
  LED13 = LED - 5mm [color="Red (633nm)" package="5 mm [THT]"]
  LED14 = LED - 5mm [color="Red (633nm)" package="5 mm [THT]"]
  LED15 = LED - 5mm [color="Red (633nm)" package="5 mm [THT]"]
  LED16 = LED - 5mm [color="Red (633nm)" package="5 mm [THT]"]
  D2 = Diode [package=diode-1n4001]
  LED17 = LED - 3mm [color="Red (633nm)" package="3 mm [THT]"]
  LED18 = LED - 3mm [color="Red (633nm)" package="3 mm [THT]"]
  LED19 = LED - 3mm [color="Red (633nm)" package="3 mm [THT]"]
  LED24 = LED - 3mm [color="Red (633nm)" package="3 mm [THT]"]
  LED22 = LED - 3mm [color="Red (633nm)" package="3 mm [THT]"]
  LED23 = LED - 3mm [color="Red (633nm)" package="3 mm [THT]"]
  LED21 = LED - 3mm [color="Red (633nm)" package="3 mm [THT]"]
  LED20 = LED - 3mm [color="Red (633nm)" package="3 mm [THT]"]
  WT5001M02-28P1 = mystery part, 28 pins [chip_label=WT5001M02-28P]
  DIP_MP3 = DIP SWITCH [package=dipswitch-02]
  PAM8403 = Header PAM8403 [form="♀ (female)" package=THT]
  EEPROM = 24LC01 [package=THT]
  C7 = Ceramic Capacitor [capacitance=100nF package="200 mil [THT, multilayer]"]
  -_L_+ = screw terminal, 2 pins
  -_R_+ = screw terminal, 2 pins
  Pot1 = POT [package=pot_alpha_rv16af-20]
  Pot2 = POT [package=pot_alpha_rv16af-20]
  Rotary_SW = Pushbutton [package=THT]
  R12 = Resistor [tolerance=±5% resistance=10k package=THT]
  SW1 = Pushbutton [package=THT]
  SW2 = Pushbutton [package=THT]
  SW3 = Pushbutton [package=THT]
  SW4 = Pushbutton [package=THT]
  SW5 = Pushbutton [package=THT]
  LCD = mystery part, 5 pins [chip_label=?]
  T1 = Transformer [package=transformer]
  T2 = Transformer [package=transformer]
  C9 = Electrolytic Capacitor [capacitance=1000µF voltage=16V package="200 mil [THT, electrolytic]"]
  C8 = Electrolytic Capacitor [capacitance=1000µF voltage=20V package="200 mil [THT, electrolytic]"]
  R13 = RPACK* [part_number=10K package=rpack-sip-pth-5]
  J1 = double row female pin header, 12 pins [form="♀ (female)"]
  Arduino_Nano = Arduino Nano (Rev3.0)
  R14 = Resistor [tolerance=±5% resistance=330 package=THT]
  R15 = Resistor [tolerance=±5% resistance=330 package=THT]
  R16 = Resistor [tolerance=±5% resistance=330 package=THT]
  R17 = Resistor [tolerance=±5% resistance=330 package=THT]
  R18 = Resistor [tolerance=±5% resistance=330 package=THT]
  R19 = Resistor [tolerance=±5% resistance=330 package=THT]
  C5 = Ceramic Capacitor [capacitance=10nF package="200 mil [THT, multilayer]"]
  C10 = Electrolytic Capacitor [capacitance=220µF voltage=16V package="100 mil [THT, electrolytic]"]

nets:
  MCU_D4: MAX7219.DIN, Arduino_Nano.D4
  dig 0: MAX7219.DIG0, LED1.cathode, LED2.cathode, LED3.cathode, LED4.cathode, LED5.cathode, LED6.cathode, LED7.cathode, LED8.cathode
  dig 4: MAX7219.DIG4, LedRing.Seg_1
  GND: MAX7219.GND, MAX7219.GND2, C1.1, C2.-, C3.-, LM7805.GND, C4.-, -5V+.GND, C6.0, Rotary.EncoderPinC, R8.Pin_0, R10.Pin_0, USB_Charger.GND, +_IN_-.pin1, USB_Battery.GND, WT5001M02-28P1.pin14, WT5001M02-28P1.pin23, PAM8403.GND#4, EEPROM.A0, EEPROM.A1, EEPROM.A2, EEPROM.0V, EEPROM.WP_-_Write_Protect, C7.1, R12.Pin_0, LCD.pin1, C9.-, C8.-, R13.1, J1.pin1, J1.pin2, J1.pin3, J1.pin4, J1.pin5, J1.pin6, Arduino_Nano.GND, C5.1, C10.-
  dig 6: MAX7219.DIG6, LedRing.Seg_3
  dig 2: MAX7219.DIG2
  dig 3: MAX7219.DIG3, LED17.cathode, LED18.cathode, LED19.cathode, LED24.cathode, LED22.cathode, LED23.cathode, LED21.cathode, LED20.cathode
  dig 7: MAX7219.DIG7, LedRing.Seg_4
  dig 5: MAX7219.DIG5, LedRing.Seg_2
  dig 1: MAX7219.DIG1, LED9.cathode, LED10.cathode, LED11.cathode, LED12.cathode, LED13.cathode, LED14.cathode, LED15.cathode, LED16.cathode
  MCU_D8: MAX7219.LOAD, Arduino_Nano.D8
  MCU_D7: MAX7219.CLK, Arduino_Nano.D7
  seg A: MAX7219.SEGA, LedRing.Led_2, LED1.anode, LED9.anode, LED17.anode
  seg F: MAX7219.SEGF, LED7.anode, LED14.anode, LED22.anode
  seg B: MAX7219.SEGB, LedRing.Led_3, LED2.anode, LED10.anode, LED18.anode
  seg G: MAX7219.SEGG, LED6.anode, LED15.anode, LED23.anode
  N1: MAX7219.ISET, R1.Pin_1
  5V/MCU_5V: MAX7219.VCC, C1.0, C2.+, R1.Pin_0, -5V+.VCC, R2.Pin_1, R3.Pin_1, R6.Pin_1, R7.Pin_1, D1.C, D2.C, DIP_MP3.4, EEPROM.+V, C7.0, Rotary_SW.leg0, SW1.leg0, SW2.leg0, SW3.leg0, SW4.leg0, SW5.leg0, LCD.pin2, Arduino_Nano.5V, C10.+
  seg C: MAX7219.SEGC, LedRing.Led_4, LED3.anode, LED11.anode, LED19.anode
  seg E: MAX7219.SEGE, LED5.anode, LED13.anode, LED21.anode
  seg dp: MAX7219.SEGDP, LedRing.Led_1, LED8.anode, LED16.anode, LED24.anode
  seg D: MAX7219.SEGD, LED4.anode, LED12.anode, LED20.anode
  N2: C3.+, LM7805.input_voltage, Sw_DC.pin2
  N3: LM7805.output_voltage, C4.+, R9.Pin_1, R11.Pin_1, USB_Charger.VBUS, D1.A
  N4: R2.Pin_0, R5.Pin_1, Rotary.EncoderPinA
  N5: R3.Pin_0, R4.Pin_0, Rotary.EncoderPinB
  MCU_D12: R4.Pin_1, C6.1, Arduino_Nano.D12/MISO
  MCU_D2: R5.Pin_0, Arduino_Nano.D2, C5.0
  I2C_SDA: R6.Pin_0, EEPROM.SDA_-_I2C_Data, LCD.pin3, Arduino_Nano.A4
  I2C_SCL: R7.Pin_0, EEPROM.SCL_-_I2C_Clock, LCD.pin4, Arduino_Nano.A5
  N6: R8.Pin_1, R9.Pin_0, USB_Charger.D+
  N7: R10.Pin_1, R11.Pin_0, USB_Charger.D-
  N8: +_IN_-.pin2, Sw_DC.pin1
  N9: USB_Battery.VBUS, Sw_Batt.pin1
  N10: Sw_Batt.pin2, D2.A
  N11: WT5001M02-28P1.pin8, T1.3, T2.4
  N12: WT5001M02-28P1.pin9, Pot2.A
  N13: WT5001M02-28P1.pin10, Pot1.A
  N14: WT5001M02-28P1.pin17, DIP_MP3.2
  N15: WT5001M02-28P1.pin22, DIP_MP3.1, PAM8403.5V, C9.+, C8.+
  MCU_TX: DIP_MP3.3, Arduino_Nano.D1/TX
  N16: PAM8403.R+, -_R_+.pin1
  N17: PAM8403.R-, -_R_+.pin2
  N18: PAM8403.L+, -_L_+.pin1
  N19: PAM8403.L-, -_L_+.pin2
  N20: PAM8403.LIN, T1.1
  N21: PAM8403.GND#9, T1.2, T2.1
  N22: PAM8403.RIN, T2.2
  N23: Pot1.S, T1.4
  N24: Pot2.S, T2.3
  N25: Rotary_SW.leg1, R12.Pin_1, Arduino_Nano.A0
  N26: SW1.leg1, R13.2, Arduino_Nano.A1
  N27: SW2.leg1, R13.3, Arduino_Nano.A2
  N28: SW3.leg1, R13.4, Arduino_Nano.A3
  N29: SW4.leg1, R13.5, Arduino_Nano.A6
  N30: SW5.leg1, R13.6, Arduino_Nano.A7
  MCU_D5: LCD.pin5, Arduino_Nano.D5
  N31: J1.pin7, R19.Pin_1
  N32: J1.pin8, R18.Pin_1
  N33: J1.pin9, R17.Pin_1
  N34: J1.pin10, R16.Pin_1
  N35: J1.pin11, R15.Pin_1
  N36: J1.pin12, R14.Pin_1
  N37: Arduino_Nano.D3, R14.Pin_0
  N38: Arduino_Nano.D6, R15.Pin_0
  N39: Arduino_Nano.D9, R16.Pin_0
  N40: Arduino_Nano.D10, R17.Pin_0
  N41: Arduino_Nano.D11/MOSI, R18.Pin_0
  MCU_3V: Arduino_Nano.3V3
  N42: Arduino_Nano.D13/SCK, R19.Pin_0

notes:
  Led driver that control multiplexed leds:
  - 16 leds of Roulette wheel,
  - 16 leds of led ring (rotary encoder)
  - 8 multipurpose leds
  + - + - + - + - + - + - + - + -
  External EEPROM
  Rotary Encoder with hardware debounce
  Microcontroller with I2C connection and 6 switches
  DC power supply:
  - 5V voltage regulator
  - USB external backup battery
  - USB charger for external battery
  MP3 player:
  - WT5001M02 module
  - 3W class D amplifier
  - dual potentiometer volume control
  - dip switch to turn off the MP3 player (to avoid problems when the skech is uploading)
  I2C LCD 20x4
  Switches
  I/O Ports
  D3-pwm
  D6-pwm
  D9-pwm
  D10-pwm
  D11-pwm
  D13
  ----- GND -----
  gnd
  vcc
  sda
  scl
  bkl
  2015-Marcelo Maximiano

custom parts:
  Generic female header - 2 pins: Generic female header
  Led ring header: Header for 16 led ring
